// Logisim project ProjectBusLayout.circ as structural Verilog: 11 circuits, main circuit Computer
module Computer (
);

  wire clock_1_out, clock_2_out, clock_3_out, cpu_1_buswriteenable, joystickcontroller_1_writetobus,
       keyboard_1_avail, keyboardcontroller_1_keyboardread, keyboardcontroller_1_writetobus,
       memorycontroller_1_writeenabletomem, memorycontroller_1_writetobus, rgb_video_1_p1, rgb_video_1_p2,
       soundcontrol_1_buzzerwriteenable, terminal_1_terminalwriteenable;
  wire [3:0] joystick_1_x, joystick_1_y;
  wire [6:0] keyboard_1_data, terminal_1_datatoterminal;
  wire [7:0] rgb_video_1_p3, rgb_video_1_p4;
  wire [13:0] soundcontrol_1_frequency;
  wire [15:0] cpu_1_addresstobus, memorycontroller_1_addresstomem;
  wire [23:0] rgb_video_1_p5;
  wire [31:0] controlled_buffer_1_out, cpu_1_datatobus, joystickcontroller_1_datatobus,
       keyboardcontroller_1_datatobus, memorycontroller_1_datatobus, memorycontroller_1_datatomem, ram_1_dout;

  RAM #(.addrWidth(16), .dataWidth(32), .enables("line")) ram_1 (
    .addr(memorycontroller_1_addresstomem), .we(memorycontroller_1_writeenabletomem), .clk(clock_1_out),
    .din(memorycontroller_1_datatomem), .dout(ram_1_dout));
  Clock clock_1 (.out(clock_1_out));
  Joystick joystick_1 (.x(joystick_1_x), .y(joystick_1_y));
  Clock clock_2 (.out(clock_2_out));
  TTY tty_1 (.data(terminal_1_datatoterminal), .clk(clock_2_out), .we(terminal_1_terminalwriteenable));  // open: clr
  Clock clock_3 (.out(clock_3_out));
  Keyboard keyboard_1 (
    .clk(clock_3_out), .re(keyboardcontroller_1_keyboardread), .avail(keyboard_1_avail),
    .data(keyboard_1_data));  // open: clr
  JoystickController joystickcontroller_1 (
    .DataToBus(joystickcontroller_1_datatobus), .WriteToBus(joystickcontroller_1_writetobus),
    .xValue(joystick_1_x), .yValue(joystick_1_y), .AddressFromBus(cpu_1_addresstobus),
    .DataFromBus(controlled_buffer_1_out), .WriteEnableFromBus(cpu_1_buswriteenable));
  Terminal terminal_1 (
    .dataToTerminal(terminal_1_datatoterminal), .TerminalWriteEnable(terminal_1_terminalwriteenable),
    .DataFromBus(controlled_buffer_1_out), .AddressFromBus(cpu_1_addresstobus),
    .WriteEnableFromBus(cpu_1_buswriteenable));
  MemoryController memorycontroller_1 (
    .DataToMem(memorycontroller_1_datatomem), .DataToBus(memorycontroller_1_datatobus),
    .WriteToBus(memorycontroller_1_writetobus), .WriteEnableToMem(memorycontroller_1_writeenabletomem),
    .AddressToMem(memorycontroller_1_addresstomem), .AddressFromBus(cpu_1_addresstobus),
    .WriteEnableFromBus(cpu_1_buswriteenable), .DataFromMem(ram_1_dout), .DataFromBus(controlled_buffer_1_out));
  assign controlled_buffer_1_out = memorycontroller_1_writetobus ? memorycontroller_1_datatobus : 32'bz;  // Controlled_Buffer controlled_buffer_1
  assign controlled_buffer_1_out = cpu_1_buswriteenable ? cpu_1_datatobus : 32'bz;  // Controlled_Buffer controlled_buffer_2
  CPU cpu_1 (
    .DataToBus(cpu_1_datatobus), .AddressToBus(cpu_1_addresstobus), .BusWriteEnable(cpu_1_buswriteenable),
    .DataFromBus(controlled_buffer_1_out));
  assign controlled_buffer_1_out = keyboardcontroller_1_writetobus ? keyboardcontroller_1_datatobus : 32'bz;  // Controlled_Buffer controlled_buffer_3
  KeyboardController keyboardcontroller_1 (
    .KeyboardRead(keyboardcontroller_1_keyboardread), .DataToBus(keyboardcontroller_1_datatobus),
    .WriteToBus(keyboardcontroller_1_writetobus), .AddressFromBus(cpu_1_addresstobus),
    .WriteEnableFromBus(cpu_1_buswriteenable), .DataFromBus(controlled_buffer_1_out),
    .KeyboardStatus(keyboard_1_avail), .KeyboardData(keyboard_1_data));
  assign controlled_buffer_1_out = joystickcontroller_1_writetobus ? joystickcontroller_1_datatobus : 32'bz;  // Controlled_Buffer controlled_buffer_4
  // RGB_Video #(.height(256), .width(256)) rgb_video_1: pin names not known; wires that end beside it: rgb_video_1_p1, rgb_video_1_p2, rgb_video_1_p3, rgb_video_1_p4, rgb_video_1_p5
  Clock clock_4 (.out(rgb_video_1_p1));
  SoundControl soundcontrol_1 (
    .buzzerWriteEnable(soundcontrol_1_buzzerwriteenable), .Frequency(soundcontrol_1_frequency),
    .AddressFromBus(cpu_1_addresstobus), .WriteEnableFromBus(cpu_1_buswriteenable),
    .DataFromBus(controlled_buffer_1_out));
  RGBController rgbcontroller_1 (
    .DataBusIn(controlled_buffer_1_out), .WriteEnable(cpu_1_buswriteenable), .AddressIn(cpu_1_addresstobus),
    .RGBX(rgb_video_1_p3), .RGBY(rgb_video_1_p4), .RGBWrite(rgb_video_1_p2), .RGBColor(rgb_video_1_p5));
  // Buzzer buzzer_1: pin names not known; wires that end beside it: soundcontrol_1_frequency, soundcontrol_1_buzzerwriteenable, 7'b0111100

  // Notes on the sheet:
  //   Write_enable
  //   Address
  //   Data
endmodule

module CPU (
  input  [31:0] DataFromBus,
  output [15:0] AddressToBus,
  output BusWriteEnable,
  output [31:0] DataToBus
);

  wire alu_1_equal, and_1_out, and_2_out, clock_1_out, control_1_aluvmemselect, control_1_anyj,
       control_1_beq, control_1_bne, control_1_immediateselect, control_1_jaljalr, control_1_jrjalr,
       control_1_reg_write_e, or_1_out;
  wire [4:0] control_1_alu_code, control_1_rd, control_1_rs, control_1_rt;
  wire [15:0] bit_extender_3_out, control_1_immediate, shifter_1_out;
  wire [25:0] bit_extender_4_out, shifter_2_out;
  wire [31:0] adder_1_out, adder_2_out, alu_1_res, bit_extender_1_out, bit_extender_2_out,
       bit_extender_5_out, multiplexer_1_out, multiplexer_2_out, multiplexer_3_out, multiplexer_4_out,
       multiplexer_5_out, multiplexer_6_out, ProgramCounter_q, regfile_1_rs_data, rom_1_data, shifter_3_out;

  Shifter #(.width(16)) shifter_1 (.in(control_1_immediate), .\dist (4'b0010), .out(shifter_1_out));
  Adder #(.width(32)) adder_1 (.a(ProgramCounter_q), .b(32'h4), .out(adder_1_out));  // open: cin, cout
  assign bit_extender_1_out = {{16{shifter_1_out[15]}}, shifter_1_out};  // Bit_Extender bit_extender_1
  Adder #(.width(32)) adder_2 (.a(adder_1_out), .b(bit_extender_1_out), .out(adder_2_out));  // open: cin, cout
  Shifter #(.width(26)) shifter_2 (.in(bit_extender_4_out), .\dist (5'b00010), .out(shifter_2_out));
  Multiplexer #(.enable("false"), .width(32)) multiplexer_1 (
    .in0(adder_1_out), .in1(adder_2_out), .out(multiplexer_1_out), .sel(or_1_out));
  assign bit_extender_2_out = {{6{shifter_2_out[25]}}, shifter_2_out};  // Bit_Extender bit_extender_2
  Multiplexer #(.enable("false"), .width(32)) multiplexer_2 (
    .in0(multiplexer_1_out), .in1(multiplexer_3_out), .out(multiplexer_2_out), .sel(control_1_anyj));
  Multiplexer #(.enable("false"), .width(32)) multiplexer_3 (
    .in0(bit_extender_2_out), .in1(regfile_1_rs_data), .out(multiplexer_3_out), .sel(control_1_jrjalr));
  or or_1 (or_1_out, and_1_out, and_2_out);
  Register #(.width(32)) ProgramCounter (
    .D(multiplexer_2_out), .en(1'b1), .clk(clock_1_out), .Q(ProgramCounter_q));  // open: clr
  Clock clock_1 (.out(clock_1_out));
  and and_1 (and_1_out, ~alu_1_equal, control_1_bne);  // AND_Gate
  and and_2 (and_2_out, alu_1_equal, control_1_beq);
  Shifter #(.shift("lr"), .width(32)) shifter_3 (.in(ProgramCounter_q), .\dist (5'b00010), .out(shifter_3_out));
  ROM #(.addrWidth(16), .dataWidth(32)) rom_1 (.addr(bit_extender_3_out), .data(rom_1_data));
  Bit_Extender #(.in_width(32)) bit_extender_3 (.in(shifter_3_out), .out(bit_extender_3_out));
  Bit_Extender #(.in_width(32), .out_width(26)) bit_extender_4 (.in(rom_1_data), .out(bit_extender_4_out));
  // Probe on rom_1_data
  Multiplexer #(.enable("false"), .width(32)) multiplexer_4 (
    .in0(alu_1_res), .in1(DataFromBus), .out(multiplexer_4_out), .sel(control_1_aluvmemselect));
  Multiplexer #(.enable("false"), .width(32)) multiplexer_5 (
    .in0(multiplexer_4_out), .in1(adder_1_out), .out(multiplexer_5_out), .sel(control_1_jaljalr));
  RegFile regfile_1 (
    .rt_data(DataToBus), .rs_data(regfile_1_rs_data), .write_e(control_1_reg_write_e), .rs(control_1_rs),
    .rd(control_1_rd), .rt(control_1_rt), .rd_data(multiplexer_5_out));
  Control control_1 (
    .rd(control_1_rd), .rs(control_1_rs), .beq(control_1_beq), .bne(control_1_bne),
    .reg_write_e(control_1_reg_write_e), .immediateSelect(control_1_immediateselect),
    .jalJalr(control_1_jaljalr), .jrJalr(control_1_jrjalr), .AnyJ(control_1_anyj),
    .ALU_code(control_1_alu_code), .rt(control_1_rt), .immediate(control_1_immediate),
    .we_mem(BusWriteEnable), .ALUvMEMselect(control_1_aluvmemselect), .Inst(rom_1_data));
  assign bit_extender_5_out = {{16{control_1_immediate[15]}}, control_1_immediate};  // Bit_Extender bit_extender_5
  Multiplexer #(.enable("false"), .width(32)) multiplexer_6 (
    .in0(DataToBus), .in1(bit_extender_5_out), .out(multiplexer_6_out), .sel(control_1_immediateselect));
  ALU alu_1 (
    .res(alu_1_res), .equal(alu_1_equal), .op1(regfile_1_rs_data), .op2(multiplexer_6_out),
    .Control(control_1_alu_code));
  Bit_Extender #(.in_width(32)) bit_extender_6 (.in(alu_1_res), .out(AddressToBus));

  // Notes on the sheet:
  //   offset: (word addressed)
  //   PC + 4
  //   label: for j, jal (word addressed)
  //   if branch is to be taken
  //   PC + 4 + Offset
  //   jr/jalr
  //   register: for jr, jalr (byte addressed)
  //   any j*
  //   1 if two registers are ==
  //   contents of rom_1 (hex, n*v repeats v):
  //   1040000f 201b000c 105b001e 201b0009 105b0015 201b000a 105b0017 201b000b 105b0016 201b0005 105bfff5
  //   201b0007 105b0009 201b0006 105b0005 3400008 201dff80 201b0000 ac1bff00 8000028 ac04ffa1 3400008
  //   8c02ffa0 10400001 ac00ffa0 3400008 8c02ff00 82d820 ac1bff00 3400008 800001e ac04ff88 3400008
  //   8c1bff80 13600003 8c02ff84 ac00ff80 3400008 1020 3400008 20100080 2011007e 20120040 2013003f
  //   20140001 20150000 2110018 2012 42080 20020009 d00c 2b020 20080001 1100005d 2002000c d00c 24820
  //   20020007 d00c 25820 200a0061 152a0006 2014ffff 20150000 2004015d 20020006 d00c 800007b 200a0064
  //   152a0006 20140001 20150000 20040105 20020006 d00c 800007b 200a0073 152a0006 20140000 20150001
  //   20040172 20020006 d00c 800007b 200a0077 152a0006 20140000 2015ffff 2004019f 20020006 d00c 800007b
  //   200a0018 156a0006 20140000 2015ffff 2004019f 20020006 d00c 800007b 200afff8 156a0006 20140000
  //   20150001 20040172 20020006 d00c 800007b 200aff81 156a0006 2014ffff 20150000 2004015d 20020006 d00c
  //   800007b 200aff8f 156a0005 20140001 20150000 20040105 20020006 d00c 2549020 2759820 2510018 5812
  //   26b5820 b5880 2cb5820 8d6c0000 200d0001 118d000e 240702a 11cd000c 212782a 11ed000a 260c02a 130d0008
  //   233c82a 132d0006 ac12ff90 ac13ff94 ac09ff98 ac00ff9c ad6d0000 8000035 20040000 20020006 d00c
  //   20040047 2002000b d00c 20040041 2002000b d00c 2004004d 2002000b d00c 20040045 2002000b d00c 20040020
  //   2002000b d00c 2004004f 2002000b d00c 20040056 2002000b d00c 20040045 2002000b d00c 20040052 2002000b
  //   d00c 20040021 2002000b d00c 20040021 2002000b d00c 20040021 2002000b d00c 20040021 2002000b d00c
  //   2002000a d00c
  //   immediate
  //   label to jump to
  //   rs-data
  //   probe to help test the value in a wire
  //   ALU
  //   MEM
  //   PC + 4
  //   jal/jalr
  //   value from memory
  //   value from ALU
endmodule

module MemoryController (
  input  [15:0] AddressFromBus,
  input  WriteEnableFromBus,
  input  [31:0] DataFromMem,
  input  [31:0] DataFromBus,
  output [15:0] AddressToMem,
  output WriteToBus,
  output WriteEnableToMem,
  output [31:0] DataToBus,
  output [31:0] DataToMem
);

  wire comparator_1_lt;

  Comparator #(.mode("unsigned"), .width(16)) comparator_1 (
    .a(AddressFromBus), .b(16'hff80), .lt(comparator_1_lt));  // open: gt, eq
  Shifter #(.shift("lr"), .width(16)) shifter_1 (.in(AddressFromBus), .\dist (4'b0010), .out(AddressToMem));
  and and_1 (WriteToBus, comparator_1_lt, ~WriteEnableFromBus);  // AND_Gate
  and and_2 (WriteEnableToMem, comparator_1_lt, WriteEnableFromBus);
  Shifter #(.shift("lr"), .width(32)) shifter_2 ();  // open: in, dist, out

  assign DataToBus = DataFromMem;
  assign DataToMem = DataFromBus;
endmodule

module KeyboardController (
  input  [31:0] DataFromBus,
  input  [15:0] AddressFromBus,
  input  WriteEnableFromBus,
  input  KeyboardStatus,
  input  [6:0] KeyboardData,
  output KeyboardRead,
  output WriteToBus,
  output [31:0] DataToBus
);

  wire and_1_out, and_3_out, comparator_1_eq, comparator_2_eq;
  wire [31:0] bit_extender_1_out, bit_extender_2_out;

  Comparator #(.width(16)) comparator_1 (.a(16'hff84), .b(AddressFromBus), .eq(comparator_1_eq));  // open: gt, lt
  Comparator #(.width(16)) comparator_2 (.a(AddressFromBus), .b(16'hff80), .eq(comparator_2_eq));  // open: gt, lt
  and and_1 (and_1_out, comparator_1_eq, ~WriteEnableFromBus);  // AND_Gate
  and and_2 (KeyboardRead, comparator_2_eq, WriteEnableFromBus);
  and and_3 (and_3_out, ~WriteEnableFromBus, comparator_2_eq);  // AND_Gate
  assign bit_extender_1_out = {{31{1'b0}}, KeyboardStatus};  // Bit_Extender bit_extender_1
  assign bit_extender_2_out = {{25{1'b0}}, KeyboardData};  // Bit_Extender bit_extender_2
  Multiplexer #(.enable("false"), .width(32)) multiplexer_1 (
    .in0(bit_extender_1_out), .in1(bit_extender_2_out), .out(DataToBus), .sel(and_1_out));
  or or_1 (WriteToBus, and_1_out, and_3_out);
endmodule

module RGBController (
  input  [31:0] DataBusIn,
  input  WriteEnable,
  input  [15:0] AddressIn,
  output [7:0] RGBX,
  output [7:0] RGBY,
  output RGBWrite,
  output [23:0] RGBColor
);

  wire and_1_out, and_2_out, and_3_out, clock_1_out, clock_2_out, clock_3_out, comparator_1_eq,
       comparator_2_eq, comparator_3_eq, comparator_4_eq;
  wire [31:0] RGB_q, xCoordinate_q, yCoordinate_q;

  Comparator #(.width(16)) comparator_1 (.a(AddressIn), .b(16'hff90), .eq(comparator_1_eq));  // open: gt, lt
  Comparator #(.width(16)) comparator_2 (.a(AddressIn), .b(16'hff94), .eq(comparator_2_eq));  // open: gt, lt
  Comparator #(.width(16)) comparator_3 (.a(AddressIn), .b(16'hff98), .eq(comparator_3_eq));  // open: gt, lt
  Comparator #(.width(16)) comparator_4 (.a(AddressIn), .b(16'hff9c), .eq(comparator_4_eq));  // open: gt, lt
  and and_1 (and_1_out, comparator_1_eq, WriteEnable);
  and and_2 (and_2_out, comparator_2_eq, WriteEnable);
  and and_3 (and_3_out, comparator_3_eq, WriteEnable);
  and and_4 (RGBWrite, comparator_4_eq, WriteEnable);
  Register #(.width(32)) xCoordinate (
    .D(DataBusIn), .en(and_1_out), .clk(clock_1_out), .Q(xCoordinate_q));  // open: clr
  Clock clock_1 (.out(clock_1_out));
  Register #(.width(32)) yCoordinate (
    .D(DataBusIn), .en(and_2_out), .clk(clock_2_out), .Q(yCoordinate_q));  // open: clr
  Clock clock_2 (.out(clock_2_out));
  Register #(.width(32)) RGB (.D(DataBusIn), .en(and_3_out), .clk(clock_3_out), .Q(RGB_q));  // open: clr
  Clock clock_3 (.out(clock_3_out));
  Bit_Extender #(.in_width(32), .out_width(8), .\type ("zero")) bit_extender_1 (.in(xCoordinate_q), .out(RGBX));
  Bit_Extender #(.in_width(32), .out_width(8), .\type ("zero")) bit_extender_2 (.in(yCoordinate_q), .out(RGBY));
  Bit_Extender #(.in_width(32), .out_width(24), .\type ("zero")) bit_extender_3 (.in(RGB_q), .out(RGBColor));
endmodule

module RegFile (
  input  [4:0] rs,
  input  [4:0] rt,
  input  [31:0] rd_data,
  input  [4:0] rd,
  input  write_e,
  output [31:0] rs_data,
  output [31:0] rt_data
);

  wire clock_1_out, clock_2_out, clock_3_out, clock_4_out, clock_5_out, clock_6_out, clock_7_out,
       clock_8_out, clock_9_out, clock_10_out, clock_11_out, clock_12_out, clock_13_out, clock_14_out,
       clock_15_out, clock_16_out, clock_17_out, clock_18_out, clock_19_out, clock_20_out, clock_21_out,
       clock_22_out, clock_23_out, clock_24_out, clock_25_out, clock_26_out, clock_27_out, clock_28_out,
       clock_29_out, clock_30_out, clock_31_out, demultiplexer_1_out0, demultiplexer_1_out1,
       demultiplexer_1_out2, demultiplexer_1_out3, demultiplexer_1_out4, demultiplexer_1_out5,
       demultiplexer_1_out6, demultiplexer_1_out7, demultiplexer_1_out8, demultiplexer_1_out9,
       demultiplexer_1_out10, demultiplexer_1_out11, demultiplexer_1_out12, demultiplexer_1_out13,
       demultiplexer_1_out14, demultiplexer_1_out15, demultiplexer_1_out16, demultiplexer_1_out17,
       demultiplexer_1_out18, demultiplexer_1_out19, demultiplexer_1_out20, demultiplexer_1_out21,
       demultiplexer_1_out22, demultiplexer_1_out23, demultiplexer_1_out24, demultiplexer_1_out25,
       demultiplexer_1_out26, demultiplexer_1_out27, demultiplexer_1_out28, demultiplexer_1_out29,
       demultiplexer_1_out30, demultiplexer_1_out31;
  wire [31:0] a0_q, a1_q, a2_q, a3_q, at_q, gp_q, k0_q, k1_q, ra_q, s0_q, s1_q, s2_q, s3_q, s4_q, s5_q, s6_q,
       s7_q, s8_q, sp_q, t0_q, t1_q, t2_q, t3_q, t4_q, t5_q, t6_q, t7_q, t8_q, t9_q, v0_q, v1_q;

  Demultiplexer #(.select(5)) demultiplexer_1 (
    .out0(demultiplexer_1_out0), .out1(demultiplexer_1_out1), .out2(demultiplexer_1_out2),
    .out3(demultiplexer_1_out3), .out4(demultiplexer_1_out4), .out5(demultiplexer_1_out5),
    .out6(demultiplexer_1_out6), .out7(demultiplexer_1_out7), .out8(demultiplexer_1_out8),
    .out9(demultiplexer_1_out9), .out10(demultiplexer_1_out10), .out11(demultiplexer_1_out11),
    .out12(demultiplexer_1_out12), .out13(demultiplexer_1_out13), .out14(demultiplexer_1_out14),
    .out15(demultiplexer_1_out15), .out16(demultiplexer_1_out16), .out17(demultiplexer_1_out17),
    .out18(demultiplexer_1_out18), .out19(demultiplexer_1_out19), .out20(demultiplexer_1_out20),
    .out21(demultiplexer_1_out21), .out22(demultiplexer_1_out22), .out23(demultiplexer_1_out23),
    .out24(demultiplexer_1_out24), .out25(demultiplexer_1_out25), .out26(demultiplexer_1_out26),
    .out27(demultiplexer_1_out27), .out28(demultiplexer_1_out28), .out29(demultiplexer_1_out29),
    .out30(demultiplexer_1_out30), .out31(demultiplexer_1_out31), .in(write_e), .sel(rd));  // open: en
  // Probe on rd_data
  Register #(.width(32)) a0 (.D(rd_data), .en(demultiplexer_1_out4), .clk(clock_1_out), .Q(a0_q));  // open: clr
  Clock clock_1 (.out(clock_1_out));
  Register #(.width(32)) t0 (.D(rd_data), .en(demultiplexer_1_out8), .clk(clock_2_out), .Q(t0_q));  // open: clr
  Clock clock_2 (.out(clock_2_out));
  Register #(.width(32)) t4 (.D(rd_data), .en(demultiplexer_1_out12), .clk(clock_3_out), .Q(t4_q));  // open: clr
  Clock clock_3 (.out(clock_3_out));
  Register #(.width(32)) s0 (.D(rd_data), .en(demultiplexer_1_out16), .clk(clock_4_out), .Q(s0_q));  // open: clr
  Clock clock_4 (.out(clock_4_out));
  Register #(.width(32)) s4 (.D(rd_data), .en(demultiplexer_1_out20), .clk(clock_5_out), .Q(s4_q));  // open: clr
  Clock clock_5 (.out(clock_5_out));
  Register #(.width(32)) t8 (.D(rd_data), .en(demultiplexer_1_out24), .clk(clock_6_out), .Q(t8_q));  // open: clr
  Clock clock_6 (.out(clock_6_out));
  Register #(.width(32)) gp (.D(rd_data), .en(demultiplexer_1_out28), .clk(clock_7_out), .Q(gp_q));  // open: clr
  Clock clock_7 (.out(clock_7_out));
  Register #(.width(32)) at (.D(rd_data), .en(demultiplexer_1_out1), .clk(clock_8_out), .Q(at_q));  // open: clr
  Clock clock_8 (.out(clock_8_out));
  Register #(.width(32)) a1 (.D(rd_data), .en(demultiplexer_1_out5), .clk(clock_9_out), .Q(a1_q));  // open: clr
  Clock clock_9 (.out(clock_9_out));
  Register #(.width(32)) t1 (.D(rd_data), .en(demultiplexer_1_out9), .clk(clock_10_out), .Q(t1_q));  // open: clr
  Clock clock_10 (.out(clock_10_out));
  Register #(.width(32)) t5 (.D(rd_data), .en(demultiplexer_1_out13), .clk(clock_11_out), .Q(t5_q));  // open: clr
  Clock clock_11 (.out(clock_11_out));
  Register #(.width(32)) s1 (.D(rd_data), .en(demultiplexer_1_out17), .clk(clock_12_out), .Q(s1_q));  // open: clr
  Clock clock_12 (.out(clock_12_out));
  Register #(.width(32)) s5 (.D(rd_data), .en(demultiplexer_1_out21), .clk(clock_13_out), .Q(s5_q));  // open: clr
  Clock clock_13 (.out(clock_13_out));
  Register #(.width(32)) t9 (.D(rd_data), .en(demultiplexer_1_out25), .clk(clock_14_out), .Q(t9_q));  // open: clr
  Clock clock_14 (.out(clock_14_out));
  Register #(.width(32)) sp (.D(rd_data), .en(demultiplexer_1_out29), .clk(clock_15_out), .Q(sp_q));  // open: clr
  Clock clock_15 (.out(clock_15_out));
  Register #(.width(32)) v0 (.D(rd_data), .en(demultiplexer_1_out2), .clk(clock_16_out), .Q(v0_q));  // open: clr
  Clock clock_16 (.out(clock_16_out));
  Register #(.width(32)) a2 (.D(rd_data), .en(demultiplexer_1_out6), .clk(clock_17_out), .Q(a2_q));  // open: clr
  Clock clock_17 (.out(clock_17_out));
  Register #(.width(32)) t2 (.D(rd_data), .en(demultiplexer_1_out10), .clk(clock_18_out), .Q(t2_q));  // open: clr
  Clock clock_18 (.out(clock_18_out));
  Register #(.width(32)) t6 (.D(rd_data), .en(demultiplexer_1_out14), .clk(clock_19_out), .Q(t6_q));  // open: clr
  Clock clock_19 (.out(clock_19_out));
  Register #(.width(32)) s2 (.D(rd_data), .en(demultiplexer_1_out18), .clk(clock_20_out), .Q(s2_q));  // open: clr
  Clock clock_20 (.out(clock_20_out));
  Register #(.width(32)) s6 (.D(rd_data), .en(demultiplexer_1_out22), .clk(clock_21_out), .Q(s6_q));  // open: clr
  Clock clock_21 (.out(clock_21_out));
  Register #(.width(32)) k0 (.D(rd_data), .en(demultiplexer_1_out26), .clk(clock_22_out), .Q(k0_q));  // open: clr
  Clock clock_22 (.out(clock_22_out));
  Register #(.width(32)) s8 (.D(rd_data), .en(demultiplexer_1_out30), .clk(clock_23_out), .Q(s8_q));  // open: clr
  Clock clock_23 (.out(clock_23_out));
  Register #(.width(32)) v1 (.D(rd_data), .en(demultiplexer_1_out3), .clk(clock_24_out), .Q(v1_q));  // open: clr
  Clock clock_24 (.out(clock_24_out));
  Register #(.width(32)) a3 (.D(rd_data), .en(demultiplexer_1_out7), .clk(clock_25_out), .Q(a3_q));  // open: clr
  Clock clock_25 (.out(clock_25_out));
  Register #(.width(32)) t3 (.D(rd_data), .en(demultiplexer_1_out11), .clk(clock_26_out), .Q(t3_q));  // open: clr
  Clock clock_26 (.out(clock_26_out));
  Register #(.width(32)) t7 (.D(rd_data), .en(demultiplexer_1_out15), .clk(clock_27_out), .Q(t7_q));  // open: clr
  Clock clock_27 (.out(clock_27_out));
  Register #(.width(32)) s3 (.D(rd_data), .en(demultiplexer_1_out19), .clk(clock_28_out), .Q(s3_q));  // open: clr
  Clock clock_28 (.out(clock_28_out));
  Register #(.width(32)) s7 (.D(rd_data), .en(demultiplexer_1_out23), .clk(clock_29_out), .Q(s7_q));  // open: clr
  Clock clock_29 (.out(clock_29_out));
  Register #(.width(32)) k1 (.D(rd_data), .en(demultiplexer_1_out27), .clk(clock_30_out), .Q(k1_q));  // open: clr
  Clock clock_30 (.out(clock_30_out));
  Register #(.width(32)) ra (.D(rd_data), .en(demultiplexer_1_out31), .clk(clock_31_out), .Q(ra_q));  // open: clr
  Clock clock_31 (.out(clock_31_out));
  Multiplexer #(.select(5), .width(32)) multiplexer_1 (
    .in0({32{1'b0}}), .in1(at_q), .in2(v0_q), .in3(v1_q), .in4(a0_q), .in5(a1_q), .in6(a2_q), .in7(a3_q),
    .in8(t0_q), .in9(t1_q), .in10(t2_q), .in11(t3_q), .in12(t4_q), .in13(t5_q), .in14(t6_q), .in15(t7_q),
    .in16(s0_q), .in17(s1_q), .in18(s2_q), .in19(s3_q), .in20(s4_q), .in21(s5_q), .in22(s6_q), .in23(s7_q),
    .in24(t8_q), .in25(t9_q), .in26(k0_q), .in27(k1_q), .in28(gp_q), .in29(sp_q), .in30(s8_q), .in31(ra_q),
    .out(rs_data), .sel(rs));  // open: en
  Multiplexer #(.select(5), .width(32)) multiplexer_2 (
    .in0({32{1'b0}}), .in1(at_q), .in2(v0_q), .in3(v1_q), .in4(a0_q), .in5(a1_q), .in6(a2_q), .in7(a3_q),
    .in8(t0_q), .in9(t1_q), .in10(t2_q), .in11(t3_q), .in12(t4_q), .in13(t5_q), .in14(t6_q), .in15(t7_q),
    .in16(s0_q), .in17(s1_q), .in18(s2_q), .in19(s3_q), .in20(s4_q), .in21(s5_q), .in22(s6_q), .in23(s7_q),
    .in24(t8_q), .in25(t9_q), .in26(k0_q), .in27(k1_q), .in28(gp_q), .in29(sp_q), .in30(s8_q), .in31(ra_q),
    .out(rt_data), .sel(rt));  // open: en
endmodule

module ALU (
  input  [4:0] Control,
  input  [31:0] op1,
  input  [31:0] op2,
  output [31:0] res,
  output equal
);

  wire clock_1_out, clock_2_out, comparator_1_lt, comparator_2_gt, comparator_2_lt, comparator_3_lt,
       comparator_4_eq, comparator_5_eq, or_2_out, or_3_out;
  wire [4:0] bit_extender_1_out, bit_extender_2_out;
  wire [31:0] adder_1_out, adder_2_out, and_1_out, bit_extender_3_out, bit_extender_4_out,
       bit_extender_5_out, bit_extender_6_out, bit_extender_7_out, divider_1_out, HI_q, LO_q,
       multiplexer_2_out, multiplier_1_out, multiplier_2_out, nor_1_out, or_1_out, shifter_1_out,
       shifter_2_out, shifter_3_out, subtractor_1_out, subtractor_2_out, xor_1_out;

  Subtractor #(.width(32)) subtractor_1 (.a(op1), .b(op2), .out(subtractor_1_out));  // open: bin, bout
  Adder #(.width(32)) adder_1 (.a(op1), .b(op2), .out(adder_1_out));  // open: cin, cout
  Divider #(.mode("twosComplement"), .width(32)) divider_1 (.a(op1), .b(op2), .out(divider_1_out));  // open: upper, rem
  Multiplier #(.width(32)) multiplier_1 (.a(op1), .b(op2), .out(multiplier_1_out));  // open: cin, cout
  Bit_Extender #(.in_width(32), .out_width(5), .\type ("zero")) bit_extender_1 (.in(op2), .out(bit_extender_1_out));
  Bit_Extender #(.in_width(32), .out_width(5), .\type ("zero")) bit_extender_2 (.in(op2), .out(bit_extender_2_out));
  Comparator #(.width(32)) comparator_1 (.a(op1), .b(op2), .eq(equal), .lt(comparator_1_lt));  // open: gt
  assign and_1_out = op1 & op2;  // AND_Gate and_1, 32 bits wide
  assign or_1_out = op1 | op2;  // OR_Gate or_1, 32 bits wide
  Comparator #(.width(32)) comparator_2 (.a(op1), .b(op2), .gt(comparator_2_gt), .lt(comparator_2_lt));  // open: eq
  assign nor_1_out = ~(op1 | op2);  // NOR_Gate nor_1, 32 bits wide
  assign xor_1_out = op1 ^ op2;  // XOR_Gate xor_1, 32 bits wide
  Shifter #(.shift("lr"), .width(32)) shifter_1 (.in(op1), .\dist (bit_extender_1_out), .out(shifter_1_out));
  Shifter #(.width(32)) shifter_2 (.in(op1), .\dist (bit_extender_2_out), .out(shifter_2_out));
  assign bit_extender_3_out = {{31{1'b0}}, comparator_1_lt};  // Bit_Extender bit_extender_3
  Adder #(.width(32)) adder_2 (.a(op1), .b(op2), .out(adder_2_out));  // open: cin, cout
  or or_2 (or_2_out, comparator_2_gt, comparator_2_lt);
  Shifter #(.shift("lr"), .width(32)) shifter_3 (.in(op2), .\dist (5'b10000), .out(shifter_3_out));
  Bit_Extender #(.in_width(32), .out_width(32), .\type ("zero")) bit_extender_4 (.in(op1), .out(bit_extender_4_out));
  Bit_Extender #(.in_width(32), .out_width(32), .\type ("zero")) bit_extender_5 (.in(op1), .out(bit_extender_5_out));
  assign bit_extender_6_out = {{31{1'b0}}, or_2_out};  // Bit_Extender bit_extender_6
  Comparator #(.width(32)) comparator_3 (
    .a(bit_extender_4_out), .b(bit_extender_5_out), .lt(comparator_3_lt));  // open: gt, eq
  assign bit_extender_7_out = {{31{1'b0}}, comparator_3_lt};  // Bit_Extender bit_extender_7
  Comparator #(.width(5)) comparator_4 (.a(Control), .b(5'b00010), .eq(comparator_4_eq));  // open: gt, lt
  Comparator #(.width(5)) comparator_5 (.a(Control), .b(5'b00011), .eq(comparator_5_eq));  // open: gt, lt
  Multiplexer #(.enable("false"), .select(5), .width(32)) multiplexer_1 (
    .in0(subtractor_1_out), .in1(adder_1_out), .in2(divider_1_out), .in3(multiplier_1_out),
    .in4(shifter_1_out), .in5(shifter_2_out), .in6(bit_extender_3_out), .in7(HI_q), .in8(LO_q),
    .in9(adder_2_out), .in10(adder_2_out), .in11(and_1_out), .in12(or_1_out), .in13(bit_extender_6_out),
    .in14(nor_1_out), .in15(xor_1_out), .in16(and_1_out), .in17(or_1_out), .in18(xor_1_out),
    .in19(shifter_3_out), .in20(bit_extender_7_out), .out(res), .sel(Control));  // open: in21, in22, in23, in24, in25, in26, in27, in28, in29, in30, in31
  or or_3 (or_3_out, comparator_4_eq, comparator_5_eq);
  Subtractor #(.width(32)) subtractor_2 (.a(op1), .b(multiplier_2_out), .out(subtractor_2_out));  // open: bin, bout
  Multiplier #(.width(32)) multiplier_2 (.a(op2), .b(res), .out(multiplier_2_out));  // open: cin, cout
  Register #(.width(32)) HI (.D(multiplexer_2_out), .en(or_3_out), .clk(clock_1_out), .Q(HI_q));  // open: clr
  Multiplexer #(.enable("false"), .width(32)) multiplexer_2 (
    .in0({32{1'b0}}), .in1(subtractor_2_out), .out(multiplexer_2_out), .sel(comparator_4_eq));
  Clock clock_1 (.out(clock_1_out));
  Register #(.width(32)) LO (.D(res), .en(or_3_out), .clk(clock_2_out), .Q(LO_q));  // open: clr
  Clock clock_2 (.out(clock_2_out));
endmodule

module Control (
  input  [31:0] Inst,
  output beq,
  output bne,
  output jalJalr,
  output AnyJ,
  output jrJalr,
  output reg_write_e,
  output [4:0] rd,
  output [4:0] rt,
  output [4:0] rs,
  output immediateSelect,
  output we_mem,
  output ALUvMEMselect,
  output [15:0] immediate,
  output [4:0] ALU_code
);

  wire and_1_out, and_2_out, and_3_out, and_4_out, and_5_out, and_6_out, and_7_out, and_8_out, and_9_out,
       and_10_out, and_11_out, and_12_out, and_13_out, and_14_out, and_15_out, and_16_out, and_17_out,
       and_18_out, comparator_1_eq, comparator_2_eq, comparator_3_eq, comparator_6_eq, comparator_7_eq,
       comparator_8_eq, comparator_9_eq, comparator_10_eq, comparator_13_eq, comparator_14_eq,
       comparator_15_eq, comparator_16_eq, comparator_17_eq, comparator_18_eq, comparator_19_eq,
       comparator_20_eq, comparator_21_eq, comparator_22_eq, comparator_23_eq, comparator_24_eq,
       comparator_25_eq, comparator_26_eq, comparator_27_eq, comparator_28_eq, comparator_29_eq,
       comparator_30_eq, comparator_31_eq, comparator_32_eq, or_1_out, or_2_out, or_3_out, or_4_out;
  wire [4:0] multiplexer_1_out, multiplexer_3_out, multiplexer_4_out, multiplexer_5_out, multiplexer_8_out,
       multiplexer_9_out, multiplexer_10_out, multiplexer_11_out, multiplexer_12_out, multiplexer_13_out,
       multiplexer_14_out, multiplexer_15_out, multiplexer_16_out, multiplexer_17_out, multiplexer_18_out,
       multiplexer_19_out, multiplexer_20_out, multiplexer_21_out, multiplexer_22_out, multiplexer_23_out,
       multiplexer_24_out, multiplexer_25_out, multiplexer_26_out, multiplexer_27_out;
  wire [15:0] bit_extender_1_out;

  // Probe on Inst[5:0]
  // Probe on Inst[10:6]
  // Probe on Inst[31:26]
  Comparator #(.width(6)) comparator_1 (.a(Inst[31:26]), .b(6'b001000), .eq(comparator_1_eq));  // open: gt, lt
  Comparator #(.width(6)) comparator_2 (.a(Inst[31:26]), .b(6'b000101), .eq(comparator_2_eq));  // open: gt, lt
  Comparator #(.width(6)) comparator_3 (.a(Inst[31:26]), .b(6'b000100), .eq(comparator_3_eq));  // open: gt, lt
  Comparator #(.width(6)) comparator_4 (.a(Inst[31:26]), .b(6'b101011), .eq(we_mem));  // open: gt, lt
  Comparator #(.width(6)) comparator_5 (.a(Inst[31:26]), .b(6'b100011), .eq(ALUvMEMselect));  // open: gt, lt
  Comparator #(.width(6)) comparator_6 (.a(Inst[31:26]), .b(6'b001100), .eq(comparator_6_eq));  // open: gt, lt
  Comparator #(.width(6)) comparator_7 (.a(Inst[31:26]), .b(6'b001101), .eq(comparator_7_eq));  // open: gt, lt
  Comparator #(.width(6)) comparator_8 (.a(Inst[31:26]), .b(6'b001110), .eq(comparator_8_eq));  // open: gt, lt
  Comparator #(.width(6)) comparator_9 (.a(Inst[31:26]), .b(6'b001111), .eq(comparator_9_eq));  // open: gt, lt
  assign bit_extender_1_out = {{11{1'b0}}, Inst[10:6]};  // Bit_Extender bit_extender_1
  Multiplexer #(.enable("false"), .width(5)) multiplexer_1 (
    .in0(Inst[15:11]), .in1(Inst[20:16]), .out(multiplexer_1_out), .sel(or_1_out));
  or or_1 (or_1_out, comparator_1_eq, comparator_9_eq);
  or or_2 (or_2_out, comparator_9_eq, comparator_8_eq, ALUvMEMselect, we_mem, comparator_3_eq, comparator_2_eq, comparator_1_eq, comparator_7_eq, comparator_6_eq);
  Multiplexer #(.enable("false"), .width(16)) multiplexer_2 (
    .in0(bit_extender_1_out), .in1(Inst[15:0]), .out(immediate), .sel(or_2_out));
  Multiplexer #(.enable("false"), .width(5)) multiplexer_3 (
    .in0(Inst[25:21]), .in1(Inst[20:16]), .out(multiplexer_3_out), .sel(or_3_out));
  Multiplexer #(.enable("false"), .width(5)) multiplexer_4 (
    .in0(multiplexer_1_out), .in1(Inst[20:16]), .out(multiplexer_4_out), .sel(ALUvMEMselect));
  Comparator #(.width(6)) comparator_10 (.a(Inst[31:26]), .b({6{1'b0}}), .eq(comparator_10_eq));  // open: gt, lt
  Multiplexer #(.enable("false"), .width(5)) multiplexer_5 (
    .in0(multiplexer_4_out), .in1({5{1'b1}}), .out(multiplexer_5_out), .sel(comparator_14_eq));
  Multiplexer #(.enable("false"), .width(5)) multiplexer_6 (
    .in0(multiplexer_5_out), .in1(5'b11010), .out(rd), .sel(and_1_out));
  Multiplexer #(.enable("false"), .width(5)) multiplexer_7 (
    .in0(multiplexer_3_out), .in1({5{1'b0}}), .out(rs), .sel(and_1_out));
  or or_3 (or_3_out, and_11_out, and_10_out);
  Comparator #(.width(6)) comparator_11 (.a(Inst[31:26]), .b(6'b000100), .eq(beq));  // open: gt, lt
  Comparator #(.width(6)) comparator_12 (.a(Inst[31:26]), .b(6'b000101), .eq(bne));  // open: gt, lt
  Comparator #(.width(6)) comparator_13 (.a(Inst[31:26]), .b(6'b000010), .eq(comparator_13_eq));  // open: gt, lt
  Comparator #(.width(6)) comparator_14 (.a(Inst[31:26]), .b(6'b000011), .eq(comparator_14_eq));  // open: gt, lt
  Comparator #(.width(6)) comparator_15 (.a(Inst[5:0]), .b(6'b001100), .eq(comparator_15_eq));  // open: gt, lt
  Comparator #(.width(6)) comparator_16 (.a(Inst[5:0]), .b(6'b001000), .eq(comparator_16_eq));  // open: gt, lt
  Comparator #(.width(6)) comparator_17 (.a(Inst[5:0]), .b(6'b001001), .eq(comparator_17_eq));  // open: gt, lt
  Comparator #(.width(6)) comparator_18 (.a(Inst[5:0]), .b(6'b100000), .eq(comparator_18_eq));  // open: gt, lt
  Comparator #(.width(6)) comparator_19 (.a(Inst[5:0]), .b(6'b100010), .eq(comparator_19_eq));  // open: gt, lt
  Comparator #(.width(6)) comparator_20 (.a(Inst[5:0]), .b(6'b011000), .eq(comparator_20_eq));  // open: gt, lt
  Comparator #(.width(6)) comparator_21 (.a(Inst[5:0]), .b(6'b011010), .eq(comparator_21_eq));  // open: gt, lt
  Comparator #(.width(6)) comparator_22 (.a(Inst[5:0]), .b(6'b010010), .eq(comparator_22_eq));  // open: gt, lt
  Comparator #(.width(6)) comparator_23 (.a(Inst[5:0]), .b(6'b010000), .eq(comparator_23_eq));  // open: gt, lt
  Comparator #(.width(6)) comparator_24 (.a(Inst[5:0]), .b({6{1'b0}}), .eq(comparator_24_eq));  // open: gt, lt
  Comparator #(.width(6)) comparator_25 (.a(Inst[5:0]), .b(6'b000010), .eq(comparator_25_eq));  // open: gt, lt
  Comparator #(.width(6)) comparator_26 (.a(Inst[5:0]), .b(6'b101010), .eq(comparator_26_eq));  // open: gt, lt
  Comparator #(.width(6)) comparator_27 (.a(Inst[5:0]), .b(6'b100100), .eq(comparator_27_eq));  // open: gt, lt
  Comparator #(.width(6)) comparator_28 (.a(Inst[5:0]), .b(6'b100101), .eq(comparator_28_eq));  // open: gt, lt
  Comparator #(.width(6)) comparator_29 (.a(Inst[5:0]), .b(6'b000001), .eq(comparator_29_eq));  // open: gt, lt
  Comparator #(.width(6)) comparator_30 (.a(Inst[5:0]), .b(6'b100111), .eq(comparator_30_eq));  // open: gt, lt
  Comparator #(.width(6)) comparator_31 (.a(Inst[5:0]), .b(6'b100110), .eq(comparator_31_eq));  // open: gt, lt
  Comparator #(.width(6)) comparator_32 (.a(Inst[5:0]), .b(6'b101011), .eq(comparator_32_eq));  // open: gt, lt
  or or_4 (or_4_out, and_4_out, comparator_1_eq);
  and and_1 (and_1_out, comparator_15_eq, comparator_10_eq);
  and and_2 (and_2_out, comparator_16_eq, comparator_10_eq);
  and and_3 (and_3_out, comparator_17_eq, comparator_10_eq);
  and and_4 (and_4_out, comparator_18_eq, comparator_10_eq);
  and and_5 (and_5_out, comparator_19_eq, comparator_10_eq);
  and and_6 (and_6_out, comparator_20_eq, comparator_10_eq);
  and and_7 (and_7_out, comparator_21_eq, comparator_10_eq);
  and and_8 (and_8_out, comparator_22_eq, comparator_10_eq);
  and and_9 (and_9_out, comparator_23_eq, comparator_10_eq);
  and and_10 (and_10_out, comparator_24_eq, comparator_10_eq);
  and and_11 (and_11_out, comparator_25_eq, comparator_10_eq);
  and and_12 (and_12_out, comparator_26_eq, comparator_10_eq);
  and and_13 (and_13_out, comparator_27_eq, comparator_10_eq);
  and and_14 (and_14_out, comparator_28_eq, comparator_10_eq);
  and and_15 (and_15_out, comparator_29_eq, comparator_10_eq);
  and and_16 (and_16_out, comparator_30_eq, comparator_10_eq);
  and and_17 (and_17_out, comparator_31_eq, comparator_10_eq);
  and and_18 (and_18_out, comparator_32_eq, comparator_10_eq);
  Multiplexer #(.enable("false"), .width(5)) multiplexer_8 (
    .in0(5'b11100), .in1({5{1'b0}}), .out(multiplexer_8_out), .sel(and_5_out));
  Multiplexer #(.enable("false"), .width(5)) multiplexer_9 (
    .in0(multiplexer_8_out), .in1(5'b01000), .out(multiplexer_9_out), .sel(and_8_out));
  Multiplexer #(.enable("false"), .width(5)) multiplexer_10 (
    .in0(multiplexer_9_out), .in1(5'b00010), .out(multiplexer_10_out), .sel(and_7_out));
  Multiplexer #(.enable("false"), .width(5)) multiplexer_11 (
    .in0(multiplexer_10_out), .in1(5'b00011), .out(multiplexer_11_out), .sel(and_6_out));
  Multiplexer #(.enable("false"), .width(5)) multiplexer_12 (
    .in0(multiplexer_11_out), .in1(5'b00110), .out(multiplexer_12_out), .sel(and_12_out));
  Multiplexer #(.enable("false"), .width(5)) multiplexer_13 (
    .in0(multiplexer_12_out), .in1(5'b00101), .out(multiplexer_13_out), .sel(and_10_out));
  Multiplexer #(.enable("false"), .width(5)) multiplexer_14 (
    .in0(multiplexer_13_out), .in1(5'b00100), .out(multiplexer_14_out), .sel(and_11_out));
  or or_5 (reg_write_e, and_1_out, comparator_14_eq, and_3_out, and_4_out, and_5_out, and_8_out, and_9_out, comparator_1_eq, and_10_out, and_11_out, and_12_out, and_13_out, and_14_out, and_15_out, and_16_out, and_17_out, and_18_out, ALUvMEMselect, comparator_9_eq, comparator_8_eq, comparator_7_eq, comparator_6_eq);
  Multiplexer #(.enable("false"), .width(5)) multiplexer_15 (
    .in0(multiplexer_14_out), .in1(5'b00111), .out(multiplexer_15_out), .sel(and_9_out));
  Multiplexer #(.enable("false"), .width(5)) multiplexer_16 (
    .in0(multiplexer_15_out), .in1(5'b00001), .out(multiplexer_16_out), .sel(or_4_out));
  Multiplexer #(.enable("false"), .width(5)) multiplexer_17 (
    .in0(multiplexer_16_out), .in1(5'b01001), .out(multiplexer_17_out), .sel(ALUvMEMselect));
  Multiplexer #(.enable("false"), .width(5)) multiplexer_18 (
    .in0(multiplexer_17_out), .in1(5'b01010), .out(multiplexer_18_out), .sel(we_mem));
  Multiplexer #(.enable("false"), .width(5)) multiplexer_19 (
    .in0(multiplexer_18_out), .in1(5'b01011), .out(multiplexer_19_out), .sel(and_13_out));
  or or_6 (immediateSelect, comparator_13_eq, comparator_14_eq, comparator_1_eq, and_10_out, and_11_out, we_mem, ALUvMEMselect, comparator_9_eq, comparator_8_eq, comparator_7_eq, comparator_6_eq);
  Multiplexer #(.enable("false"), .width(5)) multiplexer_20 (
    .in0(multiplexer_19_out), .in1(5'b01100), .out(multiplexer_20_out), .sel(and_14_out));
  Multiplexer #(.enable("false"), .width(5)) multiplexer_21 (
    .in0(multiplexer_20_out), .in1(5'b01101), .out(multiplexer_21_out), .sel(and_15_out));
  Multiplexer #(.enable("false"), .width(5)) multiplexer_22 (
    .in0(multiplexer_21_out), .in1(5'b01110), .out(multiplexer_22_out), .sel(and_16_out));
  or or_7 (jalJalr, comparator_14_eq, and_1_out, and_3_out);
  or or_8 (jrJalr, and_1_out, and_2_out, and_3_out);
  Multiplexer #(.enable("false"), .width(5)) multiplexer_23 (
    .in0(multiplexer_22_out), .in1(5'b01111), .out(multiplexer_23_out), .sel(and_17_out));
  Multiplexer #(.enable("false"), .width(5)) multiplexer_24 (
    .in0(multiplexer_23_out), .in1(5'b10000), .out(multiplexer_24_out), .sel(comparator_9_eq));
  Multiplexer #(.enable("false"), .width(5)) multiplexer_25 (
    .in0(multiplexer_24_out), .in1(5'b10001), .out(multiplexer_25_out), .sel(comparator_8_eq));
  Multiplexer #(.enable("false"), .width(5)) multiplexer_26 (
    .in0(multiplexer_25_out), .in1(5'b10010), .out(multiplexer_26_out), .sel(comparator_7_eq));
  Multiplexer #(.enable("false"), .width(5)) multiplexer_27 (
    .in0(multiplexer_26_out), .in1(5'b10011), .out(multiplexer_27_out), .sel(comparator_6_eq));
  or or_9 (AnyJ, jalJalr, comparator_13_eq, jrJalr);
  Multiplexer #(.enable("false"), .width(5)) multiplexer_28 (
    .in0(multiplexer_27_out), .in1(5'b10100), .out(ALU_code), .sel(and_18_out));

  assign rt = Inst[20:16];
endmodule

module Terminal (
  input  WriteEnableFromBus,
  input  [15:0] AddressFromBus,
  input  [31:0] DataFromBus,
  output TerminalWriteEnable,
  output [6:0] dataToTerminal
);

  wire comparator_1_eq;

  Comparator #(.width(16)) comparator_1 (.a(16'hff88), .b(AddressFromBus), .eq(comparator_1_eq));  // open: gt, lt
  Bit_Extender #(.in_width(32), .out_width(7)) bit_extender_1 (.in(DataFromBus), .out(dataToTerminal));
  and and_1 (TerminalWriteEnable, WriteEnableFromBus, comparator_1_eq);
endmodule

module JoystickController (
  input  [31:0] DataFromBus,
  input  [15:0] AddressFromBus,
  input  WriteEnableFromBus,
  input  [3:0] xValue,
  input  [3:0] yValue,
  output WriteToBus,
  output [31:0] DataToBus
);

  wire comparator_1_eq;

  Comparator #(.width(16)) comparator_1 (.a(16'hffa0), .b(AddressFromBus), .eq(comparator_1_eq));  // open: gt, lt
  assign DataToBus = {{24{yValue[3]}}, {yValue, xValue}};  // Bit_Extender bit_extender_1
  and and_1 (WriteToBus, comparator_1_eq, ~WriteEnableFromBus);  // AND_Gate
endmodule

module SoundControl (
  input  WriteEnableFromBus,
  input  [15:0] AddressFromBus,
  input  [31:0] DataFromBus,
  output buzzerWriteEnable,
  output [13:0] Frequency
);

  wire and_1_out, clock_1_out, comparator_1_eq, not_1_out, not_2_out;
  wire [13:0] bit_extender_1_out;

  Comparator #(.width(16)) comparator_1 (.a(16'hffa1), .b(AddressFromBus), .eq(comparator_1_eq));  // open: gt, lt
  and and_1 (and_1_out, WriteEnableFromBus, comparator_1_eq);
  Bit_Extender #(.in_width(32), .out_width(14)) bit_extender_1 (.in(DataFromBus), .out(bit_extender_1_out));
  not not_1 (not_1_out, and_1_out);
  not not_2 (not_2_out, not_1_out);
  Register #(.width(14)) register_1 (
    .D(bit_extender_1_out), .en(and_1_out), .clk(clock_1_out), .Q(Frequency));  // open: clr
  Clock clock_1 (.out(clock_1_out));
  not not_3 (buzzerWriteEnable, not_2_out);
endmodule
